# Fritzing sketch Drink Lantern (saved by Fritzing 0.8.7b)
circuit board: 5.80903cm x 5.82784cm
breadboards: 1

parts:
  R1 = Resistor [tolerance=±5% resistance=100k package=THT]
  R2 = Resistor [tolerance=±5% resistance=3.3 package=THT]
  Q3-CBE = NPN-Transistor [part_number="Adafruit PID756" package="TO92 [THT]"]
  Q2-GDS = Basic FET N-Channel [part_number="Adafruit PID 355" package="TO220 [THT]"]
  S1 = Pushbutton [package="[THT]"]
  S2 = Pushbutton [package="[THT]"]
  S3 = Pushbutton [package="[THT]"]
  +LED- = LED - 5mm [color="White (6500K)" package="5 mm [THT]"]
  +VCC- = Battery
  S4 = Toggle Switch [package=THT]
  Pad1 = Pad [width=24.0449786666667 height=29.3453426666667 connect=center]  # not connected

nets:
  N1: R1.Pin_0, S1.Pin_3, S1.Pin_4, +LED-.cathode
  N2: R1.Pin_1, Q3-CBE.C, Q2-GDS.gate
  N3: R2.Pin_0, Q3-CBE.B, Q2-GDS.source
  N4: R2.Pin_1, Q3-CBE.E, S4.L1
  N5: Q2-GDS.drain, +LED-.anode
  N6: S1.Pin_1, S1.Pin_2, +VCC-.+
  N7: S2.Pin_1, S2.Pin_2
  N8: S2.Pin_3, S2.Pin_4
  N9: S3.Pin_1, S3.Pin_2
  N10: S3.Pin_3, S3.Pin_4
  N11: +VCC-.-, S4.COM
